// Logisim project cpu.circ as structural Verilog: 2 circuits, main circuit main
module main (
  input  [1:0] OperandB,
  input  [1:0] StoreOp,
  input  [1:0] OperandA,
  input  [7:0] ImmOp,
  input  CLK,
  input  Subtract,
  input  BitNAND
);

  wire decoder_1_out0, decoder_1_out1, decoder_1_out2, decoder_1_out3, decoder_2_out0, decoder_2_out1,
       decoder_2_out2, decoder_2_out3, decoder_3_out0, decoder_3_out1, decoder_3_out2;
  wire [7:0] alu_1_result, controlled_buffer_1_out, controlled_buffer_2_out, RegA_q, RegB_q, RegC_q;

  ROM #(.addrWidth(16)) rom_1 ();  // open: addr, data
  Register RegA (.D(alu_1_result), .en(decoder_3_out0), .clk(CLK), .Q(RegA_q));  // open: clr
  assign controlled_buffer_1_out = decoder_1_out0 ? RegA_q : 8'bz;  // Controlled_Buffer controlled_buffer_1
  assign controlled_buffer_2_out = decoder_2_out0 ? RegA_q : 8'bz;  // Controlled_Buffer controlled_buffer_2
  Decoder #(.select(2)) decoder_1 (
    .out0(decoder_1_out0), .out1(decoder_1_out1), .out2(decoder_1_out2), .out3(decoder_1_out3), .sel(OperandA));  // open: en
  Register RegB (.D(alu_1_result), .en(decoder_3_out1), .clk(CLK), .Q(RegB_q));  // open: clr
  assign controlled_buffer_1_out = decoder_1_out1 ? RegB_q : 8'bz;  // Controlled_Buffer controlled_buffer_3
  assign controlled_buffer_2_out = decoder_2_out1 ? RegB_q : 8'bz;  // Controlled_Buffer controlled_buffer_4
  Register RegC (.D(alu_1_result), .en(decoder_3_out2), .clk(CLK), .Q(RegC_q));  // open: clr
  Decoder #(.select(2)) decoder_2 (
    .out0(decoder_2_out0), .out1(decoder_2_out1), .out2(decoder_2_out2), .out3(decoder_2_out3), .sel(OperandB));  // open: en
  assign controlled_buffer_1_out = decoder_1_out2 ? RegC_q : 8'bz;  // Controlled_Buffer controlled_buffer_5
  assign controlled_buffer_2_out = decoder_2_out2 ? RegC_q : 8'bz;  // Controlled_Buffer controlled_buffer_6
  RAM #(.addrWidth(16)) ram_1 ();  // open: addr, we, oe, clk, din, dout
  Decoder #(.select(2)) decoder_3 (
    .out0(decoder_3_out0), .out1(decoder_3_out1), .out2(decoder_3_out2), .sel(StoreOp));  // open: out3, en
  assign controlled_buffer_1_out = decoder_1_out3 ? ImmOp : 8'bz;  // Controlled_Buffer controlled_buffer_7
  assign controlled_buffer_2_out = decoder_2_out3 ? ImmOp : 8'bz;  // Controlled_Buffer controlled_buffer_8
  ALU alu_1 (
    .A(controlled_buffer_1_out), .B(controlled_buffer_2_out), .Subtract(Subtract), .BitNAND(BitNAND),
    .Result(alu_1_result));
endmodule

module ALU (
  input  [7:0] A,
  input  [7:0] B,
  input  Subtract,
  input  BitNAND,
  output [7:0] Result
);

  wire [7:0] adder_1_out, nand_1_out, xor_1_out;

  xor xor_1 (xor_1_out[0], B[0], Subtract);
  xor xor_2 (xor_1_out[1], B[1], Subtract);
  xor xor_3 (xor_1_out[2], B[2], Subtract);
  xor xor_4 (xor_1_out[3], B[3], Subtract);
  nand nand_1 (nand_1_out[0], A[0], B[0]);
  nand nand_2 (nand_1_out[1], A[1], B[1]);
  nand nand_3 (nand_1_out[2], A[2], B[2]);
  nand nand_4 (nand_1_out[3], A[3], B[3]);
  xor xor_5 (xor_1_out[4], B[4], Subtract);
  xor xor_6 (xor_1_out[5], B[5], Subtract);
  xor xor_7 (xor_1_out[6], B[6], Subtract);
  xor xor_8 (xor_1_out[7], B[7], Subtract);
  nand nand_5 (nand_1_out[4], A[4], B[4]);
  nand nand_6 (nand_1_out[5], A[5], B[5]);
  nand nand_7 (nand_1_out[6], A[6], B[6]);
  nand nand_8 (nand_1_out[7], A[7], B[7]);
  Adder adder_1 (.a(A), .b(xor_1_out), .out(adder_1_out), .cin(Subtract));  // open: cout
  Multiplexer #(.width(8)) multiplexer_1 (.in0(adder_1_out), .in1(nand_1_out), .out(Result), .sel(BitNAND));
endmodule
